// Digital circuit fetch.dig as structural Verilog
module fetch (
  input  C,
  output [15:0] instr
);

  wire [5:0] PC_out;
  wire [15:0] ramdualport_1_d;

  Counter #(.Bits(6)) PC (.en(1'b1), .C(C), .clr(1'b0), .out(PC_out));  // open: ovf
  RAMDualPort #(.AddrBits(6), .isProgramMemory("true"), .Bits(16)) ramdualport_1 (
    .A(PC_out), .Din({16{1'b0}}), .str(1'b0), .C(C), .ld(1'b1), .D(ramdualport_1_d));
  Register #(.Bits(16)) IR (.D(ramdualport_1_d), .C(C), .en(1'b1), .Q(instr));
endmodule
